// Logisim project SomaBits.circ as structural Verilog: 3 circuits, main circuit main
module main (
  input  in_1,
  input  [7:0] A,
  input  [7:0] B,
  input  OP,
  output [7:0] R,
  output Overflow__com_sinal,
  output Overflow__sem_sinal
);

  wire somador_1_out_5;
  wire [7:0] xor_1_out;

  assign xor_1_out = B ^ {8{in_1}};  // XOR_Gate xor_1, 8 bits wide
  somador somador_1 (
    .in_2(A), .C_in(in_1), .out_4(R), .in_3(xor_1_out), .out_5(somador_1_out_5), .out_6(Overflow__sem_sinal));
  xor xor_2 (Overflow__com_sinal, somador_1_out_5, Overflow__sem_sinal);

  assign OP = in_1;
endmodule

module somabits (
  input  A,
  input  B,
  input  C_in,
  output S,
  output C_out
);

  wire and_1_out, and_2_out, xor_1_out;

  xor xor_1 (xor_1_out, A, B);
  and and_1 (and_1_out, A, B);
  and and_2 (and_2_out, xor_1_out, C_in);
  xor xor_2 (S, xor_1_out, C_in);
  or or_1 (C_out, and_2_out, and_1_out);
endmodule

module somador (
  input  C_in,
  input  [7:0] in_2,
  input  [7:0] in_3,
  output [7:0] out_4,
  output out_5,
  output out_6
);

  wire somabits_1_c_out, somabits_2_c_out, somabits_3_c_out, somabits_4_c_out, somabits_5_c_out,
       somabits_6_c_out;

  somabits somabits_1 (.A(in_2[0]), .B(in_3[0]), .C_in(C_in), .S(out_4[0]), .C_out(somabits_1_c_out));
  somabits somabits_2 (.A(in_2[1]), .B(in_3[1]), .C_in(somabits_1_c_out), .S(out_4[1]), .C_out(somabits_2_c_out));
  somabits somabits_3 (.A(in_2[2]), .B(in_3[2]), .C_in(somabits_2_c_out), .S(out_4[2]), .C_out(somabits_3_c_out));
  somabits somabits_4 (.A(in_2[3]), .B(in_3[3]), .C_in(somabits_3_c_out), .S(out_4[3]), .C_out(somabits_4_c_out));
  somabits somabits_5 (.A(in_2[4]), .B(in_3[4]), .C_in(somabits_4_c_out), .S(out_4[4]), .C_out(somabits_5_c_out));
  somabits somabits_6 (.A(in_2[5]), .B(in_3[5]), .C_in(somabits_5_c_out), .S(out_4[5]), .C_out(somabits_6_c_out));
  somabits somabits_7 (.A(in_2[6]), .B(in_3[6]), .C_in(somabits_6_c_out), .S(out_4[6]), .C_out(out_5));
  somabits somabits_8 (.A(in_2[7]), .B(in_3[7]), .C_in(out_5), .S(out_4[7]), .C_out(out_6));
endmodule
