// Logisim project somador.circ as structural Verilog: 3 circuits, main circuit main
module main (
  input  [7:0] A,
  input  [7:0] B,
  input  OP,
  output overflow__sem_sinal,
  output overflow__com_sinal,
  output [7:0] R
);

  wire somador_c7, somador_c8;
  wire [7:0] xor_1_out;

  somador somador (.c0(OP), .c7(somador_c7), .c8(somador_c8), .A(A), .B(xor_1_out), .S(R));
  assign xor_1_out = {8{OP}} ^ B;  // XOR_Gate xor_1, 8 bits wide
  xor xor_2 (overflow__com_sinal, somador_c8, somador_c7);
  xor xor_3 (overflow__sem_sinal, OP, somador_c8);

  // Notes on the sheet:
  //   Gabriel Schwartz, 5486096, gschwartz@usp.br
  //   Lourenço Bogo, 11208005, louhmsb@usp.br
  //   Julia Leite, 1122 1797, julia.lsilva@usp.br
  //   Parte 1: Circuito Somador
  //   Circuito para adição e subtração de números de 8 bits
endmodule

module somador (
  input  [7:0] A,
  input  [7:0] B,
  input  c0,
  output c7,
  output c8,
  output [7:0] S
);

  wire somabits_1_c_out, somabits_2_c_out, somabits_3_c_out, somabits_4_c_out, somabits_5_c_out,
       somabits_6_c_out;

  somabits somabits_1 (.A(A[0]), .B(B[0]), .C_in(c0), .S(S[0]), .C_out(somabits_1_c_out));
  somabits somabits_2 (.A(A[1]), .B(B[1]), .C_in(somabits_1_c_out), .S(S[1]), .C_out(somabits_2_c_out));
  somabits somabits_3 (.A(A[2]), .B(B[2]), .C_in(somabits_2_c_out), .S(S[2]), .C_out(somabits_3_c_out));
  somabits somabits_4 (.A(A[3]), .B(B[3]), .C_in(somabits_3_c_out), .S(S[3]), .C_out(somabits_4_c_out));
  somabits somabits_5 (.A(A[4]), .B(B[4]), .C_in(somabits_4_c_out), .S(S[4]), .C_out(somabits_5_c_out));
  somabits somabits_6 (.A(A[5]), .B(B[5]), .C_in(somabits_5_c_out), .S(S[5]), .C_out(somabits_6_c_out));
  somabits somabits_7 (.A(A[6]), .B(B[6]), .C_in(somabits_6_c_out), .S(S[6]), .C_out(c7));
  somabits somabits_8 (.A(A[7]), .B(B[7]), .C_in(c7), .S(S[7]), .C_out(c8));
endmodule

module somabits (
  input  A,
  input  B,
  input  C_in,
  output S,
  output C_out
);

  wire and_1_out, and_2_out, xor_1_out;

  xor xor_1 (xor_1_out, A, B);
  and and_1 (and_1_out, A, B);
  and and_2 (and_2_out, xor_1_out, C_in);
  xor xor_2 (S, xor_1_out, C_in);
  or or_1 (C_out, and_2_out, and_1_out);
endmodule
